// Logisim project PROJ.circ as structural Verilog: 4 circuits, main circuit main
module main (
);

  wire alu_1_flag_0, button_1_out, button_2_out, button_3_out, dipswitch_4_sw2;
  wire [7:0] registers_1_bus_out, undriven, undriven_2, undriven_3;

  // DipSwitch dipswitch_1: pin names not known
  // DipSwitch dipswitch_2: pin names not known
  Button button_1 (.out(button_1_out));
  Button button_2 (.out(button_2_out));
  Button button_3 (.out(button_3_out));
  REGISTERS registers_1 (
    .REGISTERS_WR(undriven), .BUS_IN(registers_1_bus_out), .REGISTERS_OE(undriven_2),
    .BUS_OUT(registers_1_bus_out));
  ALU alu_1 (
    .in_1(registers_1_bus_out), .ALU1_WR(button_1_out), .ALU2_WR(button_2_out), .ALU_OE(button_3_out),
    .ALU_DATA(registers_1_bus_out), .FLAG_0(alu_1_flag_0));
  LED led_1 (.in(alu_1_flag_0));
  // DipSwitch dipswitch_3: pin names not known
  assign registers_1_bus_out = dipswitch_4_sw2 ? undriven_3 : 8'bz;  // Controlled_Buffer controlled_buffer_1
  DipSwitch #(.number(2)) dipswitch_4 (.sw2(dipswitch_4_sw2));  // open: sw1
  DotMatrix #(.inputtype("row"), .matrixcols(8), .matrixrows(1)) dotmatrix_1 (.row0(registers_1_bus_out));
endmodule

module ALU (
  input  [7:0] in_1,
  input  ALU1_WR,
  input  ALU2_WR,
  input  ALU_OE,
  output [7:0] ALU_DATA,
  output FLAG_0
);

  wire or_1_out;
  wire [7:0] adder_1_out, ALU1_q, ALU2_q, controlled_buffer_1_out;

  or or_1 (or_1_out, ALU2_WR, ALU1_WR);
  Register #(.trigger("falling")) ALU1 (
    .D(controlled_buffer_1_out), .en(1'b1), .clk(ALU1_WR), .Q(ALU1_q));  // open: clr
  Register #(.trigger("falling")) ALU2 (
    .D(controlled_buffer_1_out), .en(1'b1), .clk(ALU2_WR), .Q(ALU2_q));  // open: clr
  Adder adder_1 (.a(ALU1_q), .b(ALU2_q), .out(adder_1_out));  // open: cin, cout
  assign controlled_buffer_1_out = ALU_OE ? adder_1_out : 8'bz;  // Controlled_Buffer controlled_buffer_1
  assign controlled_buffer_1_out = or_1_out ? in_1 : 8'bz;  // Controlled_Buffer controlled_buffer_2
  Comparator comparator_1 (.a(adder_1_out), .b({8{1'b0}}), .eq(FLAG_0));  // open: gt, lt
  assign ALU_DATA = ALU_OE ? controlled_buffer_1_out : 8'bz;  // Controlled_Buffer controlled_buffer_3
endmodule

module REGISTERS (
  input  [7:0] REGISTERS_WR,
  input  [7:0] BUS_IN,
  input  [7:0] REGISTERS_OE,
  output [7:0] BUS_OUT
);

  wire or_1_out, or_2_out, undriven;
  wire [7:0] controlled_buffer_1_out, register_1_q, register_2_q, register_3_q, register_4_q, register_5_q,
       register_6_q, register_7_q, register_8_q;

  Register #(.trigger("falling")) register_1 (
    .D(controlled_buffer_1_out), .en(1'b1), .clk(REGISTERS_WR[0]), .Q(register_1_q), .clr(undriven));
  Register #(.trigger("falling")) register_2 (
    .D(controlled_buffer_1_out), .en(1'b1), .clk(REGISTERS_WR[1]), .Q(register_2_q), .clr(undriven));
  Register #(.trigger("falling")) register_3 (
    .D(controlled_buffer_1_out), .en(1'b1), .clk(REGISTERS_WR[2]), .Q(register_3_q), .clr(undriven));
  Register #(.trigger("falling")) register_4 (
    .D(controlled_buffer_1_out), .en(1'b1), .clk(REGISTERS_WR[3]), .Q(register_4_q), .clr(undriven));
  Register #(.trigger("falling")) register_5 (
    .D(controlled_buffer_1_out), .en(1'b1), .clk(REGISTERS_WR[4]), .Q(register_5_q), .clr(undriven));
  Register #(.trigger("falling")) register_6 (
    .D(controlled_buffer_1_out), .en(1'b1), .clk(REGISTERS_WR[5]), .Q(register_6_q), .clr(undriven));
  Register #(.trigger("falling")) register_7 (
    .D(controlled_buffer_1_out), .en(1'b1), .clk(REGISTERS_WR[6]), .Q(register_7_q), .clr(undriven));
  Register #(.trigger("falling")) register_8 (
    .D(controlled_buffer_1_out), .en(1'b1), .clk(REGISTERS_WR[7]), .Q(register_8_q), .clr(undriven));
  or or_1 (or_1_out, REGISTERS_WR[0], REGISTERS_WR[1], REGISTERS_WR[2], REGISTERS_WR[3], REGISTERS_WR[4], REGISTERS_WR[5], REGISTERS_WR[6], REGISTERS_WR[7]);
  assign controlled_buffer_1_out = REGISTERS_OE[0] ? register_1_q : 8'bz;  // Controlled_Buffer controlled_buffer_1
  assign controlled_buffer_1_out = REGISTERS_OE[1] ? register_2_q : 8'bz;  // Controlled_Buffer controlled_buffer_2
  assign controlled_buffer_1_out = REGISTERS_OE[2] ? register_3_q : 8'bz;  // Controlled_Buffer controlled_buffer_3
  assign controlled_buffer_1_out = REGISTERS_OE[3] ? register_4_q : 8'bz;  // Controlled_Buffer controlled_buffer_4
  assign controlled_buffer_1_out = REGISTERS_OE[4] ? register_5_q : 8'bz;  // Controlled_Buffer controlled_buffer_5
  assign controlled_buffer_1_out = REGISTERS_OE[5] ? register_6_q : 8'bz;  // Controlled_Buffer controlled_buffer_6
  assign controlled_buffer_1_out = REGISTERS_OE[6] ? register_7_q : 8'bz;  // Controlled_Buffer controlled_buffer_7
  assign controlled_buffer_1_out = REGISTERS_OE[7] ? register_8_q : 8'bz;  // Controlled_Buffer controlled_buffer_8
  assign controlled_buffer_1_out = or_1_out ? BUS_IN : 8'bz;  // Controlled_Buffer controlled_buffer_9
  assign BUS_OUT = or_2_out ? controlled_buffer_1_out : 8'bz;  // Controlled_Buffer controlled_buffer_10
  or or_2 (or_2_out, REGISTERS_OE[7], REGISTERS_OE[6], REGISTERS_OE[5], REGISTERS_OE[4], REGISTERS_OE[3], REGISTERS_OE[2], REGISTERS_OE[1], REGISTERS_OE[0]);
endmodule

module ROM_1 (
  input  [7:0] ROM_BE,
  input  ROM_OE,
  output [7:0] ROM_BD
);

  wire [7:0] rom_1_data;

  ROM rom_1 (.addr(ROM_BE), .data(rom_1_data));
  assign ROM_BD = ROM_OE ? rom_1_data : 8'bz;  // Controlled_Buffer controlled_buffer_1
endmodule
